// Logisim project 23-59.circ as structural Verilog: 3 circuits, main circuit main
module main (
);

  _3_input u_3_input_1 ();  // open: a, a_2, a_3, a_4, a_5, a_6, b, b_2, b_3, b_4, b_5, b_6, c, c_2, c_3, c_4, c_5, c_6, d, d_2, d_3, d_4, d_5, d_6, e, e_2, e_3, e_4, e_5, e_6, f, f_2, f_3, f_4, f_5, f_6, g, g_2, g_3, g_4, g_5, g_6
endmodule

module _4_input (
  input  w,
  input  x,
  input  y,
  input  z,
  output a,
  output b,
  output c,
  output d,
  output e,
  output f,
  output g
);

  wire and_1_out, and_2_out, and_3_out, and_4_out, and_5_out, and_6_out, and_7_out, and_8_out, and_9_out,
       and_10_out, and_11_out, and_12_out, and_13_out, and_14_out, and_15_out, and_16_out, and_17_out,
       not_1_out, not_2_out, not_3_out, not_4_out, not_5_out, not_6_out, not_7_out, not_8_out, not_9_out,
       not_10_out, not_11_out, not_12_out, not_13_out, not_14_out, not_15_out, not_16_out, not_17_out,
       not_18_out, not_19_out, not_20_out, not_21_out, or_1_out, or_2_out, or_3_out, or_4_out, or_6_out,
       or_8_out, or_9_out, or_10_out, or_11_out, or_14_out, or_15_out;

  not not_1 (not_1_out, x);
  not not_2 (not_2_out, z);
  not not_3 (not_3_out, y);
  not not_4 (not_4_out, z);
  not not_5 (not_5_out, y);
  not not_6 (not_6_out, x);
  not not_7 (not_7_out, z);
  not not_8 (not_8_out, x);
  not not_9 (not_9_out, y);
  not not_10 (not_10_out, x);
  not not_11 (not_11_out, z);
  not not_12 (not_12_out, z);
  not not_13 (not_13_out, y);
  not not_14 (not_14_out, z);
  not not_15 (not_15_out, y);
  not not_16 (not_16_out, z);
  not not_17 (not_17_out, x);
  not not_18 (not_18_out, y);
  not not_19 (not_19_out, z);
  and and_1 (and_1_out, not_1_out, not_2_out);
  or or_1 (or_1_out, and_1_out, y);
  and and_2 (and_2_out, x, z);
  or or_2 (or_2_out, and_2_out, w);
  not not_20 (not_20_out, x);
  or or_3 (or_3_out, not_20_out, and_3_out);
  and and_3 (and_3_out, not_3_out, not_4_out);
  and and_4 (and_4_out, y, z);
  or or_4 (or_4_out, not_5_out, z);
  or or_5 (c, or_4_out, x);
  and and_5 (and_5_out, not_6_out, not_7_out);
  or or_6 (or_6_out, and_5_out, and_6_out);
  and and_6 (and_6_out, not_8_out, y);
  and and_7 (and_7_out, y, not_21_out);
  not not_21 (not_21_out, z);
  and and_8 (and_8_out, x, not_9_out);
  and and_9 (and_9_out, and_8_out, z);
  and and_10 (and_10_out, not_10_out, not_11_out);
  or or_7 (e, and_10_out, and_11_out);
  and and_11 (and_11_out, y, not_12_out);
  and and_12 (and_12_out, not_13_out, not_14_out);
  or or_8 (or_8_out, and_12_out, and_13_out);
  and and_13 (and_13_out, x, not_15_out);
  and and_14 (and_14_out, x, not_16_out);
  or or_9 (or_9_out, and_14_out, w);
  and and_15 (and_15_out, not_17_out, y);
  or or_10 (or_10_out, and_15_out, and_16_out);
  and and_16 (and_16_out, x, not_18_out);
  and and_17 (and_17_out, x, not_19_out);
  or or_11 (or_11_out, and_17_out, w);
  or or_12 (a, or_1_out, or_2_out);
  or or_13 (b, or_3_out, and_4_out);
  or or_14 (or_14_out, or_6_out, and_7_out);
  or or_15 (or_15_out, and_9_out, w);
  or or_16 (f, or_8_out, or_9_out);
  or or_17 (g, or_10_out, or_11_out);
  or or_18 (d, or_14_out, or_15_out);
endmodule

module _3_input (
  output a,
  output a_2,
  output a_3,
  output a_4,
  output a_5,
  output a_6,
  output b,
  output b_2,
  output b_3,
  output b_4,
  output b_5,
  output b_6,
  output c,
  output c_2,
  output c_3,
  output c_4,
  output c_5,
  output c_6,
  output d,
  output d_2,
  output d_3,
  output d_4,
  output d_5,
  output d_6,
  output e,
  output e_2,
  output e_3,
  output e_4,
  output e_5,
  output e_6,
  output f,
  output f_2,
  output f_3,
  output f_4,
  output f_5,
  output f_6,
  output g,
  output g_2,
  output g_3,
  output g_4,
  output g_5,
  output g_6
);

  wire and_1_out, and_2_out, and_3_out, and_4_out, and_5_out, and_6_out, and_7_out, and_8_out, and_9_out,
       and_10_out, and_11_out, and_12_out, and_13_out, and_14_out, and_15_out, and_16_out, and_17_out,
       and_18_out, and_19_out, and_20_out, and_21_out, and_22_out, and_23_out, and_24_out, and_25_out,
       and_26_out, and_27_out, and_28_out, and_29_out, and_30_out, and_31_out, and_32_out, and_33_out,
       and_34_out, and_35_out, and_36_out, and_37_out, and_38_out, and_39_out, and_40_out, and_41_out,
       and_42_out, and_43_out, and_44_out, and_45_out, and_46_out, and_47_out, and_48_out, and_49_out,
       and_50_out, and_51_out, and_52_out, and_53_out, and_54_out, and_55_out, and_56_out, and_57_out,
       and_58_out, and_59_out, and_60_out, and_61_out, and_62_out, and_63_out, and_64_out, and_65_out,
       and_66_out, and_67_out, and_68_out, and_69_out, and_70_out, and_71_out, and_72_out, and_73_out,
       and_74_out, and_75_out, and_76_out, and_77_out, and_78_out, and_79_out, and_80_out, and_81_out,
       and_82_out, and_83_out, and_84_out, and_85_out, and_86_out, and_87_out, and_88_out, and_89_out,
       and_90_out, and_91_out, and_92_out, and_93_out, and_94_out, and_95_out, and_96_out, and_97_out,
       and_98_out, and_99_out, and_100_out, and_101_out, and_102_out, and_103_out, and_104_out, and_105_out,
       and_106_out, and_107_out, and_108_out, and_109_out, clock_1_out, j_k_ff_1_q, j_k_ff_1_qn, j_k_ff_2_q,
       j_k_ff_2_qn, j_k_ff_3_q, j_k_ff_4_q, j_k_ff_4_qn, j_k_ff_5_q, j_k_ff_5_qn, j_k_ff_6_q, j_k_ff_6_qn,
       j_k_ff_7_q, j_k_ff_8_q, j_k_ff_8_qn, j_k_ff_9_q, j_k_ff_9_qn, j_k_ff_10_q, j_k_ff_11_q, j_k_ff_11_qn,
       j_k_ff_12_q, j_k_ff_12_qn, j_k_ff_13_q, j_k_ff_13_qn, j_k_ff_14_q, j_k_ff_15_q, j_k_ff_15_qn,
       j_k_ff_16_q, j_k_ff_16_qn, j_k_ff_17_q, j_k_ff_18_q, j_k_ff_18_qn, j_k_ff_19_q, j_k_ff_19_qn,
       j_k_ff_20_q, j_k_ff_20_qn, j_k_ff_21_q, not_1_out, not_2_out, not_3_out, not_4_out, not_5_out,
       not_6_out, not_7_out, not_8_out, not_9_out, not_10_out, not_11_out, not_12_out, not_13_out,
       not_14_out, not_15_out, not_16_out, not_17_out, not_18_out, not_19_out, not_20_out, not_21_out,
       not_22_out, not_23_out, not_24_out, not_25_out, not_26_out, not_27_out, not_28_out, not_29_out,
       not_30_out, not_31_out, not_32_out, not_33_out, not_34_out, not_35_out, not_36_out, not_37_out,
       not_38_out, not_39_out, not_40_out, not_41_out, not_42_out, not_43_out, not_44_out, not_45_out,
       not_46_out, not_47_out, not_48_out, not_49_out, not_50_out, not_51_out, not_52_out, not_53_out,
       not_54_out, not_55_out, not_56_out, not_57_out, not_58_out, not_59_out, not_60_out, not_61_out,
       not_62_out, not_63_out, not_64_out, not_65_out, not_66_out, not_67_out, not_68_out, not_69_out,
       not_70_out, not_71_out, not_72_out, not_73_out, not_74_out, not_75_out, not_76_out, not_77_out,
       not_78_out, not_79_out, not_80_out, not_81_out, not_82_out, not_83_out, not_84_out, not_85_out,
       not_86_out, not_87_out, not_88_out, not_89_out, not_90_out, not_91_out, not_92_out, not_93_out,
       not_94_out, not_95_out, not_96_out, not_97_out, not_98_out, not_99_out, not_100_out, not_101_out,
       not_102_out, not_103_out, not_104_out, not_105_out, not_106_out, not_107_out, not_108_out,
       not_109_out, not_110_out, not_111_out, not_112_out, not_113_out, not_114_out, not_115_out,
       not_116_out, not_117_out, not_118_out, not_119_out, not_120_out, not_121_out, not_122_out,
       not_123_out, not_124_out, not_125_out, not_126_out, or_1_out, or_2_out, or_3_out, or_6_out, or_7_out,
       or_10_out, or_11_out, or_15_out, or_16_out, or_17_out, or_18_out, or_20_out, or_22_out, or_23_out,
       or_24_out, or_25_out, or_28_out, or_29_out, or_33_out, or_34_out, or_35_out, or_36_out, or_39_out,
       or_40_out, or_43_out, or_45_out, or_48_out, or_49_out, or_50_out, or_51_out, or_53_out, or_55_out,
       or_56_out, or_57_out, or_58_out, or_61_out, or_62_out, or_66_out, or_67_out, or_68_out, or_71_out,
       or_72_out, or_75_out, or_76_out, or_80_out, or_81_out, or_82_out, or_83_out, or_85_out, or_87_out,
       or_88_out, or_89_out, or_90_out, or_93_out, or_94_out;

  not not_1 (not_1_out, j_k_ff_3_q);
  not not_2 (not_2_out, j_k_ff_1_q);
  not not_3 (not_3_out, j_k_ff_2_q);
  not not_4 (not_4_out, j_k_ff_1_q);
  not not_5 (not_5_out, j_k_ff_2_q);
  not not_6 (not_6_out, j_k_ff_2_q);
  not not_7 (not_7_out, j_k_ff_3_q);
  not not_8 (not_8_out, j_k_ff_1_q);
  not not_9 (not_9_out, j_k_ff_1_q);
  not not_10 (not_10_out, j_k_ff_2_q);
  not not_11 (not_11_out, j_k_ff_1_q);
  not not_12 (not_12_out, j_k_ff_2_q);
  not not_13 (not_13_out, j_k_ff_3_q);
  not not_14 (not_14_out, j_k_ff_2_q);
  and and_1 (and_1_out, not_1_out, not_2_out);
  not not_15 (not_15_out, j_k_ff_3_q);
  and and_2 (and_2_out, not_3_out, not_4_out);
  or or_1 (or_1_out, not_5_out, j_k_ff_1_q);
  not not_16 (not_16_out, j_k_ff_3_q);
  not not_17 (not_17_out, j_k_ff_1_q);
  not not_18 (not_18_out, j_k_ff_3_q);
  not not_19 (not_19_out, j_k_ff_1_q);
  and and_3 (and_3_out, j_k_ff_3_q, not_6_out);
  and and_4 (and_4_out, not_7_out, not_8_out);
  and and_5 (and_5_out, j_k_ff_2_q, not_9_out);
  and and_6 (and_6_out, not_10_out, not_11_out);
  and and_7 (and_7_out, j_k_ff_3_q, not_12_out);
  not not_20 (not_20_out, j_k_ff_1_q);
  and and_8 (and_8_out, not_13_out, j_k_ff_2_q);
  and and_9 (and_9_out, j_k_ff_3_q, not_14_out);
  not not_21 (not_21_out, j_k_ff_1_q);
  J_K_Flip_Flop j_k_ff_1 (
    .J(1'b1), .clk(or_33_out), .K(1'b1), .Q(j_k_ff_1_q), .Qn(j_k_ff_1_qn), .reset(and_18_out));  // open: preset, en
  or or_2 (or_2_out, and_1_out, j_k_ff_2_q);
  and and_10 (and_10_out, j_k_ff_3_q, j_k_ff_1_q);
  or or_3 (or_3_out, not_15_out, and_2_out);
  and and_11 (and_11_out, j_k_ff_2_q, j_k_ff_1_q);
  or or_4 (c_5, or_1_out, j_k_ff_3_q);
  and and_12 (and_12_out, not_16_out, not_17_out);
  and and_13 (and_13_out, not_18_out, j_k_ff_2_q);
  and and_14 (and_14_out, j_k_ff_2_q, not_19_out);
  and and_15 (and_15_out, and_3_out, j_k_ff_1_q);
  or or_5 (e_5, and_4_out, and_5_out);
  or or_6 (or_6_out, and_6_out, and_7_out);
  and and_16 (and_16_out, j_k_ff_3_q, not_20_out);
  or or_7 (or_7_out, and_8_out, and_9_out);
  and and_17 (and_17_out, j_k_ff_3_q, not_21_out);
  J_K_Flip_Flop j_k_ff_2 (
    .J(1'b1), .clk(j_k_ff_1_qn), .K(1'b1), .Q(j_k_ff_2_q), .Qn(j_k_ff_2_qn), .reset(and_18_out));  // open: preset, en
  or or_8 (a_5, or_2_out, and_10_out);
  or or_9 (b_5, or_3_out, and_11_out);
  or or_10 (or_10_out, and_12_out, and_13_out);
  or or_11 (or_11_out, and_14_out, and_15_out);
  or or_12 (f_5, or_6_out, and_16_out);
  or or_13 (g_5, or_7_out, and_17_out);
  or or_14 (d_3, or_10_out, or_11_out);
  J_K_Flip_Flop j_k_ff_3 (
    .J(1'b1), .clk(j_k_ff_2_qn), .K(1'b1), .Q(j_k_ff_3_q), .reset(and_18_out));  // open: Qn, preset, en
  and and_18 (and_18_out, j_k_ff_2_q, j_k_ff_6_q);
  LED led_1 (.in(j_k_ff_4_q));
  J_K_Flip_Flop j_k_ff_4 (
    .J(1'b1), .clk(and_55_out), .K(1'b1), .Q(j_k_ff_4_q), .Qn(j_k_ff_4_qn), .reset(or_33_out));  // open: preset, en
  not not_22 (not_22_out, j_k_ff_6_q);
  and and_19 (and_19_out, not_22_out, not_23_out);
  not not_23 (not_23_out, j_k_ff_4_q);
  and and_20 (and_20_out, j_k_ff_6_q, j_k_ff_4_q);
  not not_24 (not_24_out, j_k_ff_6_q);
  not not_25 (not_25_out, j_k_ff_5_q);
  and and_21 (and_21_out, not_25_out, not_26_out);
  not not_26 (not_26_out, j_k_ff_4_q);
  not not_27 (not_27_out, j_k_ff_5_q);
  or or_15 (or_15_out, not_27_out, j_k_ff_4_q);
  not not_28 (not_28_out, j_k_ff_6_q);
  and and_22 (and_22_out, not_28_out, not_29_out);
  not not_29 (not_29_out, j_k_ff_4_q);
  not not_30 (not_30_out, j_k_ff_6_q);
  and and_23 (and_23_out, not_30_out, j_k_ff_5_q);
  not not_31 (not_31_out, j_k_ff_4_q);
  and and_24 (and_24_out, j_k_ff_6_q, not_32_out);
  not not_32 (not_32_out, j_k_ff_5_q);
  not not_33 (not_33_out, j_k_ff_6_q);
  and and_25 (and_25_out, not_33_out, not_34_out);
  not not_34 (not_34_out, j_k_ff_4_q);
  and and_26 (and_26_out, j_k_ff_5_q, not_35_out);
  not not_35 (not_35_out, j_k_ff_4_q);
  not not_36 (not_36_out, j_k_ff_5_q);
  and and_27 (and_27_out, not_36_out, not_37_out);
  not not_37 (not_37_out, j_k_ff_4_q);
  and and_28 (and_28_out, j_k_ff_6_q, not_38_out);
  not not_38 (not_38_out, j_k_ff_5_q);
  and and_29 (and_29_out, j_k_ff_6_q, not_39_out);
  not not_39 (not_39_out, j_k_ff_4_q);
  not not_40 (not_40_out, j_k_ff_6_q);
  and and_30 (and_30_out, not_40_out, j_k_ff_5_q);
  and and_31 (and_31_out, j_k_ff_6_q, not_41_out);
  not not_41 (not_41_out, j_k_ff_5_q);
  and and_32 (and_32_out, j_k_ff_6_q, not_42_out);
  not not_42 (not_42_out, j_k_ff_4_q);
  or or_16 (or_16_out, and_19_out, j_k_ff_5_q);
  or or_17 (or_17_out, and_20_out, j_k_ff_7_q);
  or or_18 (or_18_out, not_24_out, and_21_out);
  and and_33 (and_33_out, j_k_ff_5_q, j_k_ff_4_q);
  or or_19 (c_2, or_15_out, j_k_ff_6_q);
  or or_20 (or_20_out, and_22_out, and_23_out);
  and and_34 (and_34_out, j_k_ff_5_q, not_31_out);
  and and_35 (and_35_out, and_24_out, j_k_ff_4_q);
  or or_21 (e_2, and_25_out, and_26_out);
  or or_22 (or_22_out, and_27_out, and_28_out);
  or or_23 (or_23_out, and_29_out, j_k_ff_7_q);
  or or_24 (or_24_out, and_30_out, and_31_out);
  or or_25 (or_25_out, and_32_out, j_k_ff_7_q);
  LED led_2 (.in(j_k_ff_5_q));
  J_K_Flip_Flop j_k_ff_5 (
    .J(1'b1), .clk(j_k_ff_4_qn), .K(1'b1), .Q(j_k_ff_5_q), .Qn(j_k_ff_5_qn), .reset(or_33_out));  // open: preset, en
  or or_26 (a_2, or_16_out, or_17_out);
  or or_27 (b_2, or_18_out, and_33_out);
  or or_28 (or_28_out, or_20_out, and_34_out);
  or or_29 (or_29_out, and_35_out, j_k_ff_7_q);
  or or_30 (f_2, or_22_out, or_23_out);
  or or_31 (g_3, or_24_out, or_25_out);
  J_K_Flip_Flop j_k_ff_6 (
    .J(1'b1), .clk(j_k_ff_5_qn), .K(1'b1), .Q(j_k_ff_6_q), .Qn(j_k_ff_6_qn), .reset(or_33_out));  // open: preset, en
  or or_32 (d_5, or_28_out, or_29_out);
  LED led_3 (.in(j_k_ff_6_q));
  J_K_Flip_Flop j_k_ff_7 (
    .J(1'b1), .clk(j_k_ff_6_qn), .K(1'b1), .Q(j_k_ff_7_q), .reset(or_33_out));  // open: Qn, preset, en
  LED led_4 (.in(j_k_ff_7_q));
  and and_36 (and_36_out, j_k_ff_7_q, j_k_ff_5_q);
  and and_37 (and_37_out, j_k_ff_6_q, j_k_ff_2_q);
  or or_33 (or_33_out, and_36_out, and_37_out);
  not not_43 (not_43_out, j_k_ff_10_q);
  not not_44 (not_44_out, j_k_ff_8_q);
  not not_45 (not_45_out, j_k_ff_9_q);
  not not_46 (not_46_out, j_k_ff_8_q);
  not not_47 (not_47_out, j_k_ff_9_q);
  not not_48 (not_48_out, j_k_ff_9_q);
  not not_49 (not_49_out, j_k_ff_10_q);
  not not_50 (not_50_out, j_k_ff_8_q);
  not not_51 (not_51_out, j_k_ff_8_q);
  not not_52 (not_52_out, j_k_ff_9_q);
  not not_53 (not_53_out, j_k_ff_8_q);
  not not_54 (not_54_out, j_k_ff_9_q);
  not not_55 (not_55_out, j_k_ff_10_q);
  not not_56 (not_56_out, j_k_ff_9_q);
  and and_38 (and_38_out, not_43_out, not_44_out);
  not not_57 (not_57_out, j_k_ff_10_q);
  and and_39 (and_39_out, not_45_out, not_46_out);
  or or_34 (or_34_out, not_47_out, j_k_ff_8_q);
  not not_58 (not_58_out, j_k_ff_10_q);
  not not_59 (not_59_out, j_k_ff_8_q);
  not not_60 (not_60_out, j_k_ff_10_q);
  not not_61 (not_61_out, j_k_ff_8_q);
  and and_40 (and_40_out, j_k_ff_10_q, not_48_out);
  and and_41 (and_41_out, not_49_out, not_50_out);
  and and_42 (and_42_out, j_k_ff_9_q, not_51_out);
  and and_43 (and_43_out, not_52_out, not_53_out);
  and and_44 (and_44_out, j_k_ff_10_q, not_54_out);
  not not_62 (not_62_out, j_k_ff_8_q);
  and and_45 (and_45_out, not_55_out, j_k_ff_9_q);
  and and_46 (and_46_out, j_k_ff_10_q, not_56_out);
  not not_63 (not_63_out, j_k_ff_8_q);
  J_K_Flip_Flop j_k_ff_8 (
    .J(1'b1), .clk(and_73_out), .K(1'b1), .Q(j_k_ff_8_q), .Qn(j_k_ff_8_qn), .reset(and_55_out));  // open: preset, en
  _7_Segment_Display u_7_segment_display_1 (.g(g_5), .f(f_5), .a(a_5), .b(b_5), .e(e_5), .d(d_3), .c(c_5));  // open: dp
  or or_35 (or_35_out, and_38_out, j_k_ff_9_q);
  and and_47 (and_47_out, j_k_ff_10_q, j_k_ff_8_q);
  or or_36 (or_36_out, not_57_out, and_39_out);
  and and_48 (and_48_out, j_k_ff_9_q, j_k_ff_8_q);
  or or_37 (c_6, or_34_out, j_k_ff_10_q);
  and and_49 (and_49_out, not_58_out, not_59_out);
  and and_50 (and_50_out, not_60_out, j_k_ff_9_q);
  and and_51 (and_51_out, j_k_ff_9_q, not_61_out);
  and and_52 (and_52_out, and_40_out, j_k_ff_8_q);
  or or_38 (e_6, and_41_out, and_42_out);
  or or_39 (or_39_out, and_43_out, and_44_out);
  and and_53 (and_53_out, j_k_ff_10_q, not_62_out);
  or or_40 (or_40_out, and_45_out, and_46_out);
  and and_54 (and_54_out, j_k_ff_10_q, not_63_out);
  J_K_Flip_Flop j_k_ff_9 (
    .J(1'b1), .clk(j_k_ff_8_qn), .K(1'b1), .Q(j_k_ff_9_q), .Qn(j_k_ff_9_qn), .reset(and_55_out));  // open: preset, en
  _7_Segment_Display u_7_segment_display_2 (.g(g_3), .f(f_2), .a(a_2), .b(b_2), .e(e_2), .d(d_5), .c(c_2));  // open: dp
  or or_41 (a_6, or_35_out, and_47_out);
  or or_42 (b_6, or_36_out, and_48_out);
  or or_43 (or_43_out, and_49_out, and_50_out);
  or or_44 (d_4, or_43_out, or_45_out);
  or or_45 (or_45_out, and_51_out, and_52_out);
  or or_46 (f_6, or_39_out, and_53_out);
  or or_47 (g_6, or_40_out, and_54_out);
  J_K_Flip_Flop j_k_ff_10 (
    .J(1'b1), .clk(j_k_ff_9_qn), .K(1'b1), .Q(j_k_ff_10_q), .reset(and_55_out));  // open: Qn, preset, en
  _7_Segment_Display u_7_segment_display_3 (.g(g_6), .f(f_6), .a(a_6), .b(b_6), .e(e_6), .d(d_4), .c(c_6));  // open: dp
  and and_55 (and_55_out, j_k_ff_9_q, j_k_ff_10_q);
  _7_Segment_Display u_7_segment_display_4 (.g(g_4), .f(f_3), .a(a_3), .b(b_3), .e(e_3), .d(d_6), .c(c_3));  // open: dp
  _7_Segment_Display u_7_segment_display_5 (.g(g_2), .f(f_4), .a(a_4), .b(b_4), .e(e_4), .d(d), .c(c_4));  // open: dp
  _7_Segment_Display u_7_segment_display_6 (.g(g), .f(f), .a(a), .b(b), .e(e), .d(d_2), .c(c));  // open: dp
  not not_64 (not_64_out, j_k_ff_13_q);
  not not_65 (not_65_out, j_k_ff_11_q);
  not not_66 (not_66_out, j_k_ff_12_q);
  not not_67 (not_67_out, j_k_ff_11_q);
  not not_68 (not_68_out, j_k_ff_12_q);
  not not_69 (not_69_out, j_k_ff_13_q);
  not not_70 (not_70_out, j_k_ff_11_q);
  not not_71 (not_71_out, j_k_ff_13_q);
  not not_72 (not_72_out, j_k_ff_12_q);
  not not_73 (not_73_out, j_k_ff_13_q);
  not not_74 (not_74_out, j_k_ff_11_q);
  not not_75 (not_75_out, j_k_ff_11_q);
  not not_76 (not_76_out, j_k_ff_12_q);
  not not_77 (not_77_out, j_k_ff_11_q);
  not not_78 (not_78_out, j_k_ff_12_q);
  not not_79 (not_79_out, j_k_ff_11_q);
  not not_80 (not_80_out, j_k_ff_13_q);
  not not_81 (not_81_out, j_k_ff_12_q);
  not not_82 (not_82_out, j_k_ff_11_q);
  LED led_5 (.in(j_k_ff_11_q));
  J_K_Flip_Flop j_k_ff_11 (
    .J(1'b1), .clk(and_91_out), .K(1'b1), .Q(j_k_ff_11_q), .Qn(j_k_ff_11_qn), .reset(and_73_out));  // open: preset, en
  and and_56 (and_56_out, not_64_out, not_65_out);
  and and_57 (and_57_out, j_k_ff_13_q, j_k_ff_11_q);
  not not_83 (not_83_out, j_k_ff_13_q);
  and and_58 (and_58_out, not_66_out, not_67_out);
  or or_48 (or_48_out, not_68_out, j_k_ff_11_q);
  and and_59 (and_59_out, not_69_out, not_70_out);
  and and_60 (and_60_out, not_71_out, j_k_ff_12_q);
  not not_84 (not_84_out, j_k_ff_11_q);
  and and_61 (and_61_out, j_k_ff_13_q, not_72_out);
  and and_62 (and_62_out, not_73_out, not_74_out);
  and and_63 (and_63_out, j_k_ff_12_q, not_75_out);
  and and_64 (and_64_out, not_76_out, not_77_out);
  and and_65 (and_65_out, j_k_ff_13_q, not_78_out);
  and and_66 (and_66_out, j_k_ff_13_q, not_79_out);
  and and_67 (and_67_out, not_80_out, j_k_ff_12_q);
  and and_68 (and_68_out, j_k_ff_13_q, not_81_out);
  and and_69 (and_69_out, j_k_ff_13_q, not_82_out);
  J_K_Flip_Flop j_k_ff_12 (
    .J(1'b1), .clk(j_k_ff_11_qn), .K(1'b1), .Q(j_k_ff_12_q), .Qn(j_k_ff_12_qn), .reset(and_73_out));  // open: preset, en
  or or_49 (or_49_out, and_56_out, j_k_ff_12_q);
  or or_50 (or_50_out, and_57_out, j_k_ff_14_q);
  or or_51 (or_51_out, not_83_out, and_58_out);
  and and_70 (and_70_out, j_k_ff_12_q, j_k_ff_11_q);
  or or_52 (c_3, or_48_out, j_k_ff_13_q);
  or or_53 (or_53_out, and_59_out, and_60_out);
  and and_71 (and_71_out, j_k_ff_12_q, not_84_out);
  and and_72 (and_72_out, and_61_out, j_k_ff_11_q);
  or or_54 (e_3, and_62_out, and_63_out);
  or or_55 (or_55_out, and_64_out, and_65_out);
  or or_56 (or_56_out, and_66_out, j_k_ff_14_q);
  or or_57 (or_57_out, and_67_out, and_68_out);
  or or_58 (or_58_out, and_69_out, j_k_ff_14_q);
  LED led_6 (.in(j_k_ff_12_q));
  or or_59 (a_3, or_49_out, or_50_out);
  or or_60 (b_3, or_51_out, and_70_out);
  or or_61 (or_61_out, or_53_out, and_71_out);
  or or_62 (or_62_out, and_72_out, j_k_ff_14_q);
  or or_63 (f_3, or_55_out, or_56_out);
  or or_64 (g_4, or_57_out, or_58_out);
  LED led_7 (.in(j_k_ff_13_q));
  J_K_Flip_Flop j_k_ff_13 (
    .J(1'b1), .clk(j_k_ff_12_qn), .K(1'b1), .Q(j_k_ff_13_q), .Qn(j_k_ff_13_qn), .reset(and_73_out));  // open: preset, en
  or or_65 (d_6, or_61_out, or_62_out);
  J_K_Flip_Flop j_k_ff_14 (
    .J(1'b1), .clk(j_k_ff_13_qn), .K(1'b1), .Q(j_k_ff_14_q), .reset(and_73_out));  // open: Qn, preset, en
  LED led_8 (.in(j_k_ff_14_q));
  and and_73 (and_73_out, j_k_ff_14_q, j_k_ff_12_q);
  not not_85 (not_85_out, j_k_ff_17_q);
  not not_86 (not_86_out, j_k_ff_15_q);
  not not_87 (not_87_out, j_k_ff_16_q);
  not not_88 (not_88_out, j_k_ff_15_q);
  not not_89 (not_89_out, j_k_ff_16_q);
  not not_90 (not_90_out, j_k_ff_16_q);
  not not_91 (not_91_out, j_k_ff_17_q);
  not not_92 (not_92_out, j_k_ff_15_q);
  not not_93 (not_93_out, j_k_ff_15_q);
  not not_94 (not_94_out, j_k_ff_16_q);
  not not_95 (not_95_out, j_k_ff_15_q);
  not not_96 (not_96_out, j_k_ff_16_q);
  not not_97 (not_97_out, j_k_ff_17_q);
  not not_98 (not_98_out, j_k_ff_16_q);
  and and_74 (and_74_out, not_85_out, not_86_out);
  not not_99 (not_99_out, j_k_ff_17_q);
  and and_75 (and_75_out, not_87_out, not_88_out);
  or or_66 (or_66_out, not_89_out, j_k_ff_15_q);
  not not_100 (not_100_out, j_k_ff_17_q);
  not not_101 (not_101_out, j_k_ff_15_q);
  not not_102 (not_102_out, j_k_ff_17_q);
  not not_103 (not_103_out, j_k_ff_15_q);
  and and_76 (and_76_out, j_k_ff_17_q, not_90_out);
  and and_77 (and_77_out, not_91_out, not_92_out);
  and and_78 (and_78_out, j_k_ff_16_q, not_93_out);
  and and_79 (and_79_out, not_94_out, not_95_out);
  and and_80 (and_80_out, j_k_ff_17_q, not_96_out);
  not not_104 (not_104_out, j_k_ff_15_q);
  and and_81 (and_81_out, not_97_out, j_k_ff_16_q);
  and and_82 (and_82_out, j_k_ff_17_q, not_98_out);
  not not_105 (not_105_out, j_k_ff_15_q);
  J_K_Flip_Flop j_k_ff_15 (
    .J(1'b1), .clk(and_109_out), .K(1'b1), .Q(j_k_ff_15_q), .Qn(j_k_ff_15_qn), .reset(and_91_out));  // open: preset, en
  or or_67 (or_67_out, and_74_out, j_k_ff_16_q);
  and and_83 (and_83_out, j_k_ff_17_q, j_k_ff_15_q);
  or or_68 (or_68_out, not_99_out, and_75_out);
  and and_84 (and_84_out, j_k_ff_16_q, j_k_ff_15_q);
  or or_69 (c_4, or_66_out, j_k_ff_17_q);
  and and_85 (and_85_out, not_100_out, not_101_out);
  and and_86 (and_86_out, not_102_out, j_k_ff_16_q);
  and and_87 (and_87_out, j_k_ff_16_q, not_103_out);
  and and_88 (and_88_out, and_76_out, j_k_ff_15_q);
  or or_70 (e_4, and_77_out, and_78_out);
  or or_71 (or_71_out, and_79_out, and_80_out);
  and and_89 (and_89_out, j_k_ff_17_q, not_104_out);
  or or_72 (or_72_out, and_81_out, and_82_out);
  and and_90 (and_90_out, j_k_ff_17_q, not_105_out);
  or or_73 (a_4, or_67_out, and_83_out);
  or or_74 (b_4, or_68_out, and_84_out);
  or or_75 (or_75_out, and_85_out, and_86_out);
  or or_76 (or_76_out, and_87_out, and_88_out);
  or or_77 (f_4, or_71_out, and_89_out);
  or or_78 (g_2, or_72_out, and_90_out);
  J_K_Flip_Flop j_k_ff_16 (
    .J(1'b1), .clk(j_k_ff_15_qn), .K(1'b1), .Q(j_k_ff_16_q), .Qn(j_k_ff_16_qn), .reset(and_91_out));  // open: preset, en
  or or_79 (d, or_75_out, or_76_out);
  J_K_Flip_Flop j_k_ff_17 (
    .J(1'b1), .clk(j_k_ff_16_qn), .K(1'b1), .Q(j_k_ff_17_q), .reset(and_91_out));  // open: Qn, preset, en
  and and_91 (and_91_out, j_k_ff_16_q, j_k_ff_17_q);
  Clock clock_1 (.out(clock_1_out));
  LED led_9 (.in(j_k_ff_18_q));
  J_K_Flip_Flop j_k_ff_18 (
    .J(1'b1), .clk(clock_1_out), .K(1'b1), .Q(j_k_ff_18_q), .Qn(j_k_ff_18_qn), .reset(and_109_out));  // open: preset, en
  not not_106 (not_106_out, j_k_ff_20_q);
  not not_107 (not_107_out, j_k_ff_18_q);
  not not_108 (not_108_out, j_k_ff_19_q);
  not not_109 (not_109_out, j_k_ff_18_q);
  not not_110 (not_110_out, j_k_ff_19_q);
  not not_111 (not_111_out, j_k_ff_20_q);
  not not_112 (not_112_out, j_k_ff_18_q);
  not not_113 (not_113_out, j_k_ff_20_q);
  not not_114 (not_114_out, j_k_ff_19_q);
  not not_115 (not_115_out, j_k_ff_20_q);
  not not_116 (not_116_out, j_k_ff_18_q);
  not not_117 (not_117_out, j_k_ff_18_q);
  not not_118 (not_118_out, j_k_ff_19_q);
  not not_119 (not_119_out, j_k_ff_18_q);
  not not_120 (not_120_out, j_k_ff_19_q);
  not not_121 (not_121_out, j_k_ff_18_q);
  not not_122 (not_122_out, j_k_ff_20_q);
  not not_123 (not_123_out, j_k_ff_19_q);
  not not_124 (not_124_out, j_k_ff_18_q);
  and and_92 (and_92_out, not_106_out, not_107_out);
  or or_80 (or_80_out, and_92_out, j_k_ff_19_q);
  and and_93 (and_93_out, j_k_ff_20_q, j_k_ff_18_q);
  or or_81 (or_81_out, and_93_out, j_k_ff_21_q);
  not not_125 (not_125_out, j_k_ff_20_q);
  or or_82 (or_82_out, not_125_out, and_94_out);
  and and_94 (and_94_out, not_108_out, not_109_out);
  and and_95 (and_95_out, j_k_ff_19_q, j_k_ff_18_q);
  or or_83 (or_83_out, not_110_out, j_k_ff_18_q);
  or or_84 (c, or_83_out, j_k_ff_20_q);
  and and_96 (and_96_out, not_111_out, not_112_out);
  or or_85 (or_85_out, and_96_out, and_97_out);
  and and_97 (and_97_out, not_113_out, j_k_ff_19_q);
  and and_98 (and_98_out, j_k_ff_19_q, not_126_out);
  not not_126 (not_126_out, j_k_ff_18_q);
  and and_99 (and_99_out, j_k_ff_20_q, not_114_out);
  and and_100 (and_100_out, and_99_out, j_k_ff_18_q);
  and and_101 (and_101_out, not_115_out, not_116_out);
  or or_86 (e, and_101_out, and_102_out);
  and and_102 (and_102_out, j_k_ff_19_q, not_117_out);
  and and_103 (and_103_out, not_118_out, not_119_out);
  or or_87 (or_87_out, and_103_out, and_104_out);
  and and_104 (and_104_out, j_k_ff_20_q, not_120_out);
  and and_105 (and_105_out, j_k_ff_20_q, not_121_out);
  or or_88 (or_88_out, and_105_out, j_k_ff_21_q);
  and and_106 (and_106_out, not_122_out, j_k_ff_19_q);
  or or_89 (or_89_out, and_106_out, and_107_out);
  and and_107 (and_107_out, j_k_ff_20_q, not_123_out);
  and and_108 (and_108_out, j_k_ff_20_q, not_124_out);
  or or_90 (or_90_out, and_108_out, j_k_ff_21_q);
  LED led_10 (.in(j_k_ff_19_q));
  J_K_Flip_Flop j_k_ff_19 (
    .J(1'b1), .clk(j_k_ff_18_qn), .K(1'b1), .Q(j_k_ff_19_q), .Qn(j_k_ff_19_qn), .reset(and_109_out));  // open: preset, en
  or or_91 (a, or_80_out, or_81_out);
  or or_92 (b, or_82_out, and_95_out);
  or or_93 (or_93_out, or_85_out, and_98_out);
  or or_94 (or_94_out, and_100_out, j_k_ff_21_q);
  or or_95 (f, or_87_out, or_88_out);
  or or_96 (g, or_89_out, or_90_out);
  or or_97 (d_2, or_93_out, or_94_out);
  LED led_11 (.in(j_k_ff_20_q));
  J_K_Flip_Flop j_k_ff_20 (
    .J(1'b1), .clk(j_k_ff_19_qn), .K(1'b1), .Q(j_k_ff_20_q), .Qn(j_k_ff_20_qn), .reset(and_109_out));  // open: preset, en
  J_K_Flip_Flop j_k_ff_21 (
    .J(1'b1), .clk(j_k_ff_20_qn), .K(1'b1), .Q(j_k_ff_21_q), .reset(and_109_out));  // open: Qn, preset, en
  LED led_12 (.in(j_k_ff_21_q));
  and and_109 (and_109_out, j_k_ff_21_q, j_k_ff_19_q);

  // Notes on the sheet:
  //   1
  //   2
  //   4
  //   8
  //   Hour
  //   Minute
  //   Second
  //   1
  //   2
  //   4
  //   8
  //   1
  //   2
  //   4
  //   8
endmodule
