// Logisim project 77 Display.circ as structural Verilog: 1 circuit, main circuit main
module main (
  input  X,
  input  Y,
  input  Z,
  input  Enable
);

  wire _0_out, _1_out, _2_out, _3_out, _4_out, _5_out, _6_out, _7_out, a_2_out, a_out, b_2_out, b_out,
       c_2_out, c_out, d_out, e_out, f_out, g_out, not_1_out, not_2_out, not_3_out;

  not not_1 (not_1_out, X);
  not not_2 (not_2_out, Y);
  not not_3 (not_3_out, Z);
  and _0 (_0_out, not_1_out, not_2_out, not_3_out, Enable);
  and _1 (_1_out, Z, not_1_out, not_2_out, Enable);
  and _2 (_2_out, Y, not_1_out, not_3_out, Enable);
  and _3 (_3_out, Y, Z, not_1_out, Enable);
  and _4 (_4_out, not_2_out, X, not_3_out, Enable);
  and _5 (_5_out, X, Z, not_2_out, Enable);
  and _6 (_6_out, X, Y, not_3_out, Enable);
  and _7 (_7_out, X, Y, Z, Enable);
  LED led_1 (.in(_0_out));
  LED led_2 (.in(_1_out));
  LED led_3 (.in(_2_out));
  LED led_4 (.in(_3_out));
  LED led_5 (.in(_4_out));
  LED led_6 (.in(_5_out));
  LED led_7 (.in(_6_out));
  LED led_8 (.in(_7_out));
  or a (a_out, _0_out, _3_out, _2_out, _5_out, _6_out);
  or b (b_out, _0_out, _2_out, _3_out, _4_out, _1_out);
  or c (c_out, _1_out, _0_out, _3_out, _4_out, _5_out);
  or d (d_out, _3_out, _2_out, _0_out, _5_out, _6_out);
  LED led_9 (.in(d_out));
  LED led_10 (.in(e_out));
  or e (e_out, _0_out, _2_out, _6_out);
  or f (f_out, _0_out, _4_out, _5_out, _6_out);
  LED led_11 (.in(f_out));
  LED led_12 (.in(g_out));
  or g (g_out, _2_out, _3_out, _4_out, _5_out, _6_out);
  or a_2 (a_2_out, _7_out, a_out);
  or b_2 (b_2_out, b_out, _7_out);
  or c_2 (c_2_out, _7_out, c_out, _6_out);
  LED led_13 (.in(a_2_out));
  LED led_14 (.in(b_2_out));
  LED led_15 (.in(c_2_out));
  _7_Segment_Display u_7_segment_display_1 (
    .g(g_out), .f(f_out), .a(a_2_out), .b(b_2_out), .e(e_out), .d(d_out), .c(c_2_out));  // open: dp

  // Notes on the sheet:
  //   4
  //   2
  //   1
endmodule
