// Logisim project MUX.circ as structural Verilog: 1 circuit, main circuit main
module main (
  input  _4,
  input  _2,
  input  _1,
  input  in_4,
  input  in_5
);

  wire _1_2_out, _1_out, _2_2_out, _2_out, _3_2_out, _3_out, _4_2_out, _4_out, not_1_out, not_2_out,
       not_3_out, or_1_out, or_2_out;

  not not_1 (not_1_out, _4);
  not not_2 (not_2_out, _2);
  not not_3 (not_3_out, _1);
  and u__1 (_1_out, not_1_out, not_2_out, _1);
  and u__2 (_2_out, not_2_out, _4, not_3_out);
  and _3 (_3_out, not_1_out, _2, not_3_out);
  and u__4 (_4_out, _4, _2, _1);
  and _1_2 (_1_2_out, not_1_out, not_2_out, in_4);
  and _2_2 (_2_2_out, not_2_out, _4, _1);
  and _3_2 (_3_2_out, not_1_out, _2, _1);
  and _4_2 (_4_2_out, _4, _2, in_5);
  or or_1 (or_1_out, _1_out, _2_out, _3_out, _4_out);
  or or_2 (or_2_out, _1_2_out, _2_2_out, _3_2_out, _4_2_out);
  LED led_1 (.in(or_1_out));
  LED led_2 (.in(or_2_out));

  // Notes on the sheet:
  //   SUM
  //   CARRY
endmodule
