// Logisim project synchronous counter.circ as structural Verilog: 1 circuit, main circuit main
module main (
);

  wire and_1_out, and_2_out, and_3_out, and_4_out, and_5_out, and_6_out, and_7_out, and_8_out, and_9_out,
       and_10_out, clock_1_out, j_k_ff_1_q, j_k_ff_1_qn, j_k_ff_2_q, j_k_ff_2_qn, j_k_ff_3_q, j_k_ff_3_qn,
       j_k_ff_4_q, j_k_ff_4_qn, or_1_out, or_2_out, or_3_out, or_4_out, or_5_out;

  or or_1 (or_1_out, and_2_out, j_k_ff_3_q);
  Clock clock_1 (.out(clock_1_out));
  and and_1 (and_1_out, j_k_ff_3_q, j_k_ff_4_qn);
  and and_2 (and_2_out, j_k_ff_2_qn, j_k_ff_1_qn);
  and and_3 (and_3_out, j_k_ff_2_q, j_k_ff_4_q);
  LED led_1 (.in(j_k_ff_1_q));
  J_K_Flip_Flop j_k_ff_1 (
    .J(and_1_out), .clk(clock_1_out), .K(and_3_out), .Q(j_k_ff_1_q), .Qn(j_k_ff_1_qn));  // open: preset, en, reset
  and and_4 (and_4_out, j_k_ff_4_qn, j_k_ff_3_qn);
  or or_2 (or_2_out, and_4_out, and_6_out);
  and and_5 (and_5_out, j_k_ff_1_q, j_k_ff_2_qn, j_k_ff_4_q);
  LED led_2 (.in(j_k_ff_2_q));
  J_K_Flip_Flop j_k_ff_2 (
    .J(or_2_out), .clk(clock_1_out), .K(or_3_out), .Q(j_k_ff_2_q), .Qn(j_k_ff_2_qn));  // open: preset, en, reset
  and and_6 (and_6_out, j_k_ff_3_q, j_k_ff_4_q);
  and and_7 (and_7_out, j_k_ff_1_q, j_k_ff_3_qn);
  or or_3 (or_3_out, and_6_out, and_7_out);
  and and_8 (and_8_out, j_k_ff_1_qn, j_k_ff_2_q);
  or or_4 (or_4_out, and_5_out, and_8_out);
  LED led_3 (.in(j_k_ff_3_q));
  J_K_Flip_Flop j_k_ff_3 (
    .J(or_4_out), .clk(clock_1_out), .K(j_k_ff_4_qn), .Q(j_k_ff_3_q), .Qn(j_k_ff_3_qn));  // open: preset, en, reset
  LED led_4 (.in(j_k_ff_4_q));
  J_K_Flip_Flop j_k_ff_4 (
    .J(or_5_out), .clk(clock_1_out), .K(or_1_out), .Q(j_k_ff_4_q), .Qn(j_k_ff_4_qn));  // open: preset, en, reset
  and and_9 (and_9_out, j_k_ff_1_q, j_k_ff_2_q);
  and and_10 (and_10_out, j_k_ff_1_qn, j_k_ff_3_qn);
  or or_5 (or_5_out, and_9_out, and_10_out);

  // Notes on the sheet:
  //   3
  //   2
  //   1
  //   0
endmodule
